// Digital circuit 2-Bit Multiplizierer.dig as structural Verilog
module _2_Bit_Multiplizierer (
  input  A4,
  input  A3,
  input  A2,
  input  A1,
  input  B2,
  input  B1
);

  wire C5, E1, E2, E3, E4, F1, F2, F3, F4, halbaddierer_1_cn, S2, S3, S4, S5, volladdierer_1_cn,
       volladdierer_2_cn;

  and and_1 (E1, A1, B1);
  and and_2 (E2, A2, B1);
  and and_3 (E3, A3, B1);
  and and_4 (E4, A4, B1);
  and and_5 (F1, A1, B2);
  and and_6 (F2, A2, B2);
  and and_7 (F3, A3, B2);
  and and_8 (F4, A4, B2);
  Halbaddierer halbaddierer_1 (.A(E2), .B(F1), .Sn(S2), .Cn(halbaddierer_1_cn));
  Volladdierer volladdierer_1 (.A(E3), .B(F2), .C(halbaddierer_1_cn), .Cn(volladdierer_1_cn), .Sn(S3));
  Volladdierer volladdierer_2 (.A(E4), .B(F3), .C(volladdierer_1_cn), .Cn(volladdierer_2_cn), .Sn(S4));
  Halbaddierer halbaddierer_2 (.A(F4), .B(volladdierer_2_cn), .Sn(S5), .Cn(C5));
  LED led_1 (.in(C5));
  LED led_2 (.in(S5));
  LED led_3 (.in(S4));
  LED led_4 (.in(S3));
  LED led_5 (.in(S2));
  LED led_6 (.in(E1));

  // Other names for the same wires on the sheet: S1 = E1
endmodule
