// Digital circuit 4-Bit-Addierer.dig as structural Verilog
module _4_Bit_Addierer (
  input  A4,
  input  A3,
  input  A2,
  input  A1,
  input  B4,
  input  B3,
  input  B2,
  input  B1,
  output S1,
  output S2,
  output S3,
  output S4,
  output C4
);

  wire C1, C2, C3;

  Halbaddierer halbaddierer_1 (.A(A1), .B(B1), .Sn(S1), .Cn(C1));
  Volladdierer volladdierer_1 (.A(A2), .B(B2), .C(C1), .Sn(S2), .Cn(C2));
  Volladdierer volladdierer_2 (.A(A3), .B(B3), .C(C2), .Sn(S3), .Cn(C3));
  Volladdierer volladdierer_3 (.A(A4), .B(B4), .C(C3), .Sn(S4), .Cn(C4));
  LED led_1 (.in(C4));
  LED led_2 (.in(S4));
  LED led_3 (.in(C3));
  LED led_4 (.in(S3));
  LED led_5 (.in(C2));
  LED led_6 (.in(S2));
  LED led_7 (.in(C1));
  LED led_8 (.in(S1));
endmodule
