// Digital circuit 4-Bit-Subtrahierer.dig as structural Verilog
module _4_Bit_Subtrahierer (
  input  A4,
  input  A3,
  input  A2,
  input  A1,
  input  B4,
  input  B3,
  input  B2,
  input  B1,
  output S1,
  output C1,
  output S2,
  output C2,
  output S3,
  output C3,
  output S4,
  output C4
);

  wire halbaddierer_1_cn, halbaddierer_1_sn, halbaddierer_2_cn, halbaddierer_2_sn, halbaddierer_3_cn,
       halbaddierer_3_sn, halbaddierer_4_sn, not_1_out, not_2_out, not_3_out, not_4_out;

  not not_1 (not_1_out, B1);
  not not_2 (not_2_out, B2);
  not not_3 (not_3_out, B3);
  not not_4 (not_4_out, B4);
  Halbaddierer halbaddierer_1 (.A(not_1_out), .B(1'b1), .Sn(halbaddierer_1_sn), .Cn(halbaddierer_1_cn));
  Halbaddierer halbaddierer_2 (.A(not_2_out), .B(halbaddierer_1_cn), .Sn(halbaddierer_2_sn), .Cn(halbaddierer_2_cn));
  Halbaddierer halbaddierer_3 (.A(not_3_out), .B(halbaddierer_2_cn), .Sn(halbaddierer_3_sn), .Cn(halbaddierer_3_cn));
  Halbaddierer halbaddierer_4 (.A(not_4_out), .B(halbaddierer_3_cn), .Sn(halbaddierer_4_sn));  // open: Cn
  Halbaddierer halbaddierer_5 (.A(A1), .B(halbaddierer_1_sn), .Sn(S1), .Cn(C1));
  Volladdierer volladdierer_1 (.A(A2), .B(halbaddierer_2_sn), .C(C1), .Sn(S2), .Cn(C2));
  Volladdierer volladdierer_2 (.A(A3), .B(halbaddierer_3_sn), .C(C2), .Sn(S3), .Cn(C3));
  Volladdierer volladdierer_3 (.A(A4), .B(halbaddierer_4_sn), .C(C3), .Sn(S4), .Cn(C4));
  LED led_1 (.in(S4));
  LED led_2 (.in(C4));
  LED led_3 (.in(S3));
  LED led_4 (.in(C3));
  LED led_5 (.in(S2));
  LED led_6 (.in(S1));
  LED led_7 (.in(C2));
  LED led_8 (.in(C1));
endmodule
