// Digital circuit Halbaddierer.dig as structural Verilog
module Halbaddierer (
  input  A,
  input  B,
  output Sn,
  output Cn
);

  wire not_1_out, not_2_out;

  not not_1 (not_1_out, A);
  not not_2 (not_2_out, B);
  xor xor_1 (Sn, A, B);
  and and_1 (Cn, A, B);
endmodule
