// Digital circuit Volladdierer.dig as structural Verilog
module Volladdierer (
  input  A,
  input  B,
  input  C,
  output Cn,
  output Sn
);

  wire halbaddierer_1_cn, halbaddierer_1_sn, halbaddierer_2_cn;

  Halbaddierer halbaddierer_1 (.A(A), .B(B), .Sn(halbaddierer_1_sn), .Cn(halbaddierer_1_cn));
  Halbaddierer halbaddierer_2 (.A(halbaddierer_1_sn), .B(C), .Sn(Sn), .Cn(halbaddierer_2_cn));
  or or_1 (Cn, halbaddierer_1_cn, halbaddierer_2_cn);
endmodule
