// Digital circuit 4-Bit Multiplizierer.dig as structural Verilog
module _4_Bit_Multiplizierer (
  input  A4,
  input  A3,
  input  A2,
  input  A1,
  input  B4,
  input  B3,
  input  B2,
  input  B1,
  input  _0,
  output S1,
  output S2,
  output S3,
  output S4,
  output S5,
  output S6,
  output S7,
  output C7
);

  wire _4_bit_addierer_1_c4, _4_bit_addierer_1_s2, _4_bit_addierer_1_s3, _4_bit_addierer_1_s4,
       _4_bit_addierer_2_c4, _4_bit_addierer_2_s2, _4_bit_addierer_2_s3, _4_bit_addierer_2_s4, E2, E3, E4,
       F1, F2, F3, F4, G1, G2, G3, G4, H1, H2, H3, H4;

  and and_1 (S1, A1, B1);
  and and_2 (E2, A2, B1);
  and and_3 (E3, A3, B1);
  and and_4 (E4, A4, B1);
  and and_5 (F1, A1, B2);
  and and_6 (F2, A2, B2);
  and and_7 (F3, A3, B2);
  and and_8 (F4, A4, B2);
  and and_9 (G1, A1, B3);
  and and_10 (G2, A2, B3);
  and and_11 (G3, A3, B3);
  and and_12 (G4, A4, B3);
  LED led_1 (.in(C7));
  and and_13 (H1, A1, B4);
  and and_14 (H2, A2, B4);
  and and_15 (H3, A3, B4);
  and and_16 (H4, A4, B4);
  LED led_2 (.in(S7));
  LED led_3 (.in(S6));
  _4_Bit_Addierer _4_bit_addierer_1 (
    .A4(F4), .A3(F3), .A2(F2), .A1(F1), .B4(_0), .B3(E4), .B2(E3), .B1(E2), .S1(S2),
    .S2(_4_bit_addierer_1_s2), .S3(_4_bit_addierer_1_s3), .S4(_4_bit_addierer_1_s4), .C4(_4_bit_addierer_1_c4));
  LED led_4 (.in(S5));
  LED led_5 (.in(S4));
  LED led_6 (.in(S3));
  _4_Bit_Addierer _4_bit_addierer_2 (
    .A4(G4), .A3(G3), .A2(G2), .A1(G1), .B4(_4_bit_addierer_1_c4), .B3(_4_bit_addierer_1_s4),
    .B2(_4_bit_addierer_1_s3), .B1(_4_bit_addierer_1_s2), .S1(S3), .S2(_4_bit_addierer_2_s2),
    .S3(_4_bit_addierer_2_s3), .S4(_4_bit_addierer_2_s4), .C4(_4_bit_addierer_2_c4));
  LED led_7 (.in(S2));
  LED led_8 (.in(S1));
  _4_Bit_Addierer _4_bit_addierer_3 (
    .A4(H4), .A3(H3), .A2(H2), .A1(H1), .B4(_4_bit_addierer_2_c4), .B3(_4_bit_addierer_2_s4),
    .B2(_4_bit_addierer_2_s3), .B1(_4_bit_addierer_2_s2), .S1(S4), .S2(S5), .S3(S6), .S4(S7), .C4(C7));

  // Other names for the same wires on the sheet: E1 = S1

  // Notes on the sheet:
  //   128
  //   64
  //   32
  //   8
  //   16
  //   4
  //   2
  //   1
endmodule
