// Digital circuit 4-Bit-Addierer-Subtrahierer.dig as structural Verilog
module _4_Bit_Addierer_Subtrahierer (
  input  A4,
  input  A3,
  input  A2,
  input  A1,
  input  B4,
  input  B3,
  input  B2,
  input  B1,
  input  Plus___Minus,
  input  \Minus_große_Zahl ,
  output S1,
  output C1,
  output S2,
  output C2,
  output S3,
  output C3,
  output S4,
  output C4
);

  wire BK1, BK2, BK3, BK4, halbaddierer_1_cn, halbaddierer_2_cn, halbaddierer_3_cn, halbaddierer_5_cn,
       halbaddierer_6_cn, halbaddierer_7_cn, S1_t, S2_t, S3_t, S4_t, xor_1_out, xor_2_out, xor_3_out,
       xor_4_out, xor_5_out, xor_6_out, xor_7_out, xor_8_out;

  xor xor_1 (xor_1_out, Plus___Minus, B1);
  xor xor_2 (xor_2_out, Plus___Minus, B2);
  xor xor_3 (xor_3_out, Plus___Minus, B3);
  xor xor_4 (xor_4_out, Plus___Minus, B4);
  Halbaddierer halbaddierer_1 (.A(xor_1_out), .B(Plus___Minus), .Sn(BK1), .Cn(halbaddierer_1_cn));
  Halbaddierer halbaddierer_2 (.A(xor_2_out), .B(halbaddierer_1_cn), .Sn(BK2), .Cn(halbaddierer_2_cn));
  Halbaddierer halbaddierer_3 (.A(xor_3_out), .B(halbaddierer_2_cn), .Sn(BK3), .Cn(halbaddierer_3_cn));
  Halbaddierer halbaddierer_4 (.A(xor_4_out), .B(halbaddierer_3_cn), .Sn(BK4));  // open: Cn
  xor xor_5 (xor_5_out, \Minus_große_Zahl , S1);
  xor xor_6 (xor_6_out, \Minus_große_Zahl , S2);
  xor xor_7 (xor_7_out, \Minus_große_Zahl , S3);
  xor xor_8 (xor_8_out, \Minus_große_Zahl , S4);
  Halbaddierer halbaddierer_5 (.A(xor_5_out), .B(\Minus_große_Zahl ), .Sn(S1_t), .Cn(halbaddierer_5_cn));
  Halbaddierer halbaddierer_6 (.A(xor_6_out), .B(halbaddierer_5_cn), .Sn(S2_t), .Cn(halbaddierer_6_cn));
  Halbaddierer halbaddierer_7 (.A(xor_7_out), .B(halbaddierer_6_cn), .Sn(S3_t), .Cn(halbaddierer_7_cn));
  Halbaddierer halbaddierer_8 (.A(xor_8_out), .B(halbaddierer_7_cn), .Sn(S4_t));  // open: Cn
  LED led_1 (.in(C4));
  LED led_2 (.in(S4_t));
  LED led_3 (.in(C3));
  LED led_4 (.in(S3_t));
  LED led_5 (.in(C2));
  LED led_6 (.in(S2_t));
  LED led_7 (.in(C1));
  LED led_8 (.in(S1_t));
  Halbaddierer halbaddierer_9 (.A(A1), .B(BK1), .Sn(S1), .Cn(C1));
  Volladdierer volladdierer_1 (.A(A2), .B(BK2), .C(C1), .Sn(S2), .Cn(C2));
  Volladdierer volladdierer_2 (.A(A3), .B(BK3), .C(C2), .Sn(S3), .Cn(C3));
  Volladdierer volladdierer_3 (.A(A4), .B(BK4), .C(C3), .Sn(S4), .Cn(C4));

  // Other names for the same wires on the sheet: plus = Plus___Minus; S1_zwischen = S1; S2_zwischen = S2;
  //   S3_zwischen = S3; S4_zwischen = S4
endmodule
