// Digital circuit Anzeige.dig as structural Verilog
module Anzeige (
  input  in_1,
  input  _1,
  input  _2,
  input  _3,
  input  _4,
  input  _5,
  input  _6,
  input  _7,
  input  _8,
  input  _9
);

  wire or_1_out, or_2_out, or_3_out, or_4_out, or_5_out, or_6_out, or_7_out;

  or or_1 (or_1_out, _2, _3, _5, _6, _7, _8, _9);
  or or_2 (or_2_out, _1, _2, _3, _4, _7, _8, _9);
  or or_3 (or_3_out, _1, _3, _4, _5, _6, _7, _8, _9);
  or or_4 (or_4_out, _2, _3, _5, _6, _8, _9);
  or or_5 (or_5_out, _2, _6, _8);
  or or_6 (or_6_out, _4, _5, _6, _8, _9);
  or or_7 (or_7_out, _2, _3, _4, _5, _6, _8, _9);
  Seven_Seg seven_seg_1 (
    .a(or_1_out), .b(or_2_out), .c(or_3_out), .d(or_4_out), .e(or_5_out), .f(or_6_out), .g(or_7_out),
    .dp(in_1));
endmodule
