// Digital circuit 3-Bit-Multiplizierer.dig as structural Verilog
module _3_Bit_Multiplizierer (
  input  A4,
  input  A3,
  input  A2,
  input  A1,
  input  B3,
  input  B2,
  input  B1,
  output S1,
  output S2,
  output S3,
  output S4,
  output S5,
  output S6,
  output C6
);

  wire and_2_out, and_3_out, and_4_out, and_5_out, and_6_out, and_7_out, and_8_out, and_9_out, and_10_out,
       and_11_out, and_12_out, halbaddierer_1_cn, halbaddierer_2_cn, volladdierer_1_cn, volladdierer_1_sn,
       volladdierer_2_cn, volladdierer_2_sn, volladdierer_3_cn, volladdierer_3_sn, volladdierer_4_cn,
       volladdierer_5_cn;

  and and_1 (S1, A1, B1);
  and and_2 (and_2_out, A2, B1);
  and and_3 (and_3_out, A3, B1);
  and and_4 (and_4_out, A4, B1);
  // _3_Bit_Multiplizierer _3_bit_multiplizierer_1: pin names not known
  and and_5 (and_5_out, A1, B2);
  and and_6 (and_6_out, A2, B2);
  and and_7 (and_7_out, A3, B2);
  and and_8 (and_8_out, A4, B2);
  Halbaddierer halbaddierer_1 (.A(and_2_out), .B(and_5_out), .Sn(S2), .Cn(halbaddierer_1_cn));
  Volladdierer volladdierer_1 (
    .A(and_6_out), .B(and_3_out), .C(halbaddierer_1_cn), .Cn(volladdierer_1_cn), .Sn(volladdierer_1_sn));
  Volladdierer volladdierer_2 (
    .A(and_4_out), .B(and_7_out), .C(volladdierer_1_cn), .Cn(volladdierer_2_cn), .Sn(volladdierer_2_sn));
  Volladdierer volladdierer_3 (
    .A(and_8_out), .B(1'b0), .C(volladdierer_2_cn), .Cn(volladdierer_3_cn), .Sn(volladdierer_3_sn));
  LED led_1 (.in(C6));
  LED led_2 (.in(S6));
  LED led_3 (.in(S5));
  LED led_4 (.in(S4));
  and and_9 (and_9_out, A1, B3);
  and and_10 (and_10_out, A2, B3);
  and and_11 (and_11_out, A3, B3);
  and and_12 (and_12_out, A4, B3);
  LED led_5 (.in(S3));
  LED led_6 (.in(S2));
  LED led_7 (.in(S1));
  Halbaddierer halbaddierer_2 (.A(volladdierer_1_sn), .B(and_9_out), .Sn(S3), .Cn(halbaddierer_2_cn));
  Volladdierer volladdierer_4 (
    .A(volladdierer_2_sn), .B(and_10_out), .C(halbaddierer_2_cn), .Cn(volladdierer_4_cn), .Sn(S4));
  Volladdierer volladdierer_5 (
    .A(and_11_out), .B(volladdierer_3_sn), .C(volladdierer_4_cn), .Cn(volladdierer_5_cn), .Sn(S5));
  Volladdierer volladdierer_6 (.A(and_12_out), .B(volladdierer_3_cn), .C(volladdierer_5_cn), .Cn(C6), .Sn(S6));
endmodule
